// Logisim project ula.circ as structural Verilog: 3 circuits, main circuit Ula
module Ula (
  input  [7:0] D0,
  input  [7:0] D1,
  input  MovHeight,
  input  [2:0] UlaCtrl,
  output UlaIn1Zero,
  output Zero,
  output [7:0] D
);

  wire or_2_out, or_3_out;
  wire [7:0] ANDL, Mov, NOTL, ORL, SL, Soma, SR, Sub;

  Adder adder_1 (.a(D0), .b(D1), .out(Soma));  // open: cin, cout
  Subtractor subtractor_1 (.a(D0), .b(D1), .out(Sub));  // open: bin, bout
  assign ANDL = D0 & D1;  // AND_Gate and_1, 8 bits wide
  assign ORL = D0 | D1;  // OR_Gate or_1, 8 bits wide
  assign NOTL = ~D1;  // NOT_Gate not_1, 8 bits wide
  Shifter shifter_1 (.in(D0), .\dist (D1[2:0]), .out(SL));
  Shifter #(.shift("lr")) shifter_2 (.in(D0), .\dist (D1[2:0]), .out(SR));
  Multiplexer #(.select(3), .width(8)) multiplexer_1 (
    .in0(Soma), .in1(Sub), .in2(ANDL), .in3(ORL), .in4(NOTL), .in5(SL), .in6(SR), .in7(Mov), .out(D),
    .sel(UlaCtrl));
  or or_2 (or_2_out, D0[0], D0[1], D0[2], D0[3], D0[4], D0[5], D0[6], D0[7]);
  or or_3 (or_3_out, Sub[0], Sub[1], Sub[2], Sub[3], Sub[4], Sub[5], Sub[6], Sub[7]);
  Multiplexer #(.width(8)) multiplexer_2 (
    .in0({D0[7:4], D1[3:0]}), .in1({D1[3:0], D0[3:0]}), .out(Mov), .sel(MovHeight));
  not not_2 (UlaIn1Zero, or_2_out);
  not not_3 (Zero, or_3_out);

  // Other names for the same wires on the sheet: MH = MovHeight
endmodule

module Registers (
  input  [1:0] Ra,
  input  [1:0] Rb,
  input  Clk,
  input  RegWrite,
  input  [7:0] Data,
  output [7:0] D0,
  output [7:0] D1,
  output [7:0] R0
);

  wire WE0, WE1, WE2, WE3;
  wire [7:0] R1, R2, R3;

  Demultiplexer #(.select(2)) demultiplexer_1 (.out0(WE0), .out1(WE1), .out2(WE2), .out3(WE3), .in(RegWrite), .sel(Ra));
  Register register_1 (.D(Data), .en(WE0), .clk(Clk), .Q(R0));  // open: clr
  Register register_2 (.D(Data), .en(WE1), .clk(Clk), .Q(R1));  // open: clr
  Register register_3 (.D(Data), .en(WE2), .clk(Clk), .Q(R2));  // open: clr
  Register register_4 (.D(Data), .en(WE3), .clk(Clk), .Q(R3));  // open: clr
  Multiplexer #(.select(2), .width(8)) multiplexer_1 (.in0(R0), .in1(R1), .in2(R2), .in3(R3), .out(D0), .sel(Ra));
  Multiplexer #(.select(2), .width(8)) multiplexer_2 (.in0(R0), .in1(R1), .in2(R2), .in3(R3), .out(D1), .sel(Rb));

  // Other names for the same wires on the sheet: D0_t[7:0] = Data; D1_t[7:0] = Data; D2[7:0] = Data; D3[7:0] = Data
endmodule

module main (
  output [15:0] out_1,
  output [1:0] out_2,
  output out_3,
  output [1:0] out_4,
  output out_5,
  output [3:0] out_6,
  output out_7,
  output [3:0] out_8,
  output [2:0] out_9,
  output out_10,
  output out_11,
  output [1:0] out_12,
  output out_13,
  output out_14,
  output out_15,
  output [7:0] out_16,
  output [7:0] out_17,
  output [7:0] out_18
);

  wire and_1_out, Clk, or_1_out, RaZero, UncJmp, Zero;
  wire [1:0] RaDef;
  wire [7:0] DetourAddr, Imm, JumpAddr, MemOut, NextAddr, op1, op2, PC, PC1, R0, UlaOut;

  ROM rom_1 (.addr(PC), .data({out_8, out_4, out_2}));
  Clock clock_1 (.out(Clk));
  Multiplexer #(.width(8)) multiplexer_1 (.in0(PC1), .in1(DetourAddr), .out(NextAddr), .sel(or_1_out));
  or or_1 (or_1_out, and_1_out, UncJmp);
  and and_1 (and_1_out, out_1[5], RaZero);
  Adder adder_1 (.a(PC), .b(8'h1), .out(PC1));  // open: cin, cout
  Adder adder_2 (.a(PC), .b(Imm), .out(JumpAddr));  // open: cin, cout
  Register register_1 (.D(NextAddr), .en(1'b1), .clk(Clk), .Q(PC));  // open: clr
  ROM #(.addrWidth(4), .dataWidth(16)) ControlSignals (.addr(out_8), .data(out_1));
  RAM #(.enables("line"), .\type ("nonvolatile")) ram_1 (
    .addr(op2), .we(out_1[10]), .oe(out_1[11]), .clk(Clk), .din(op1), .dout(MemOut));
  Registers registers_1 (
    .Ra(RaDef), .Rb(out_2), .Clk(Clk), .RegWrite(out_1[12]), .Data(out_18), .D0(op1), .D1(op2), .R0(R0));
  Multiplexer #(.width(8)) multiplexer_2 (.in0(op2), .in1(Imm), .out(out_17), .sel(out_1[6]));
  assign Imm = {{4{out_4[1]}}, {out_4, out_2}};  // Bit_Extender bit_extender_1
  and and_2 (UncJmp, out_8[1], ~out_8[2], ~out_8[3]);  // AND_Gate
  Multiplexer #(.width(8)) multiplexer_3 (.in0(JumpAddr), .in1(op2), .out(DetourAddr), .sel(out_1[0]));
  Ula ula_1 (
    .D0(out_16), .D1(out_17), .MovHeight(out_1[2]), .UlaCtrl(out_1[9:7]), .UlaIn1Zero(RaZero), .Zero(Zero),
    .D(UlaOut));
  Multiplexer #(.select(2), .width(8)) multiplexer_4 (
    .in0(UlaOut), .in1(MemOut), .in2(op2), .out(out_18), .sel(out_1[4:3]));  // open: in3
  Multiplexer #(.width(2)) multiplexer_5 (.in0(2'b00), .in1(out_4), .out(RaDef), .sel(out_1[1]));
  Multiplexer #(.width(8)) multiplexer_6 (.in0(R0), .in1(op1), .out(out_16), .sel(out_1[1]));

  assign out_3 = out_1[12];
  assign out_5 = out_1[11];
  assign out_6 = {out_4, out_2};
  assign out_7 = out_1[10];
  assign out_9 = out_1[9:7];
  assign out_10 = out_1[6];
  assign out_11 = out_1[5];
  assign out_12 = out_1[4:3];
  assign out_13 = out_1[2];
  assign out_14 = out_1[1];
  assign out_15 = out_1[0];

  // Other names for the same wires on the sheet: Data[7:0] = out_18; Imm4bits[3:0] = {out_4, out_2};
  //   Inst[7:0] = {out_8, out_4, out_2}; Rb[1:0] = out_2; Ra[1:0] = out_4; opcode[3:0] = out_8; JmpSrc = out_1[0];
  //   Signals[15:0] = out_1; RegSrc = out_1[1]; MoveHeight = out_1[2]; MemToReg[1:0] = out_1[4:3]; PcScr = out_1[5];
  //   UlaSrc = out_1[6]; UlaCtrl[2:0] = out_1[9:7]; MemWrite = out_1[10]; MemRead = out_1[11]; RegWrite = out_1[12];
  //   UlaIn1[7:0] = out_16; UlaIn2[7:0] = out_17

  // Notes on the sheet:
  //   contents of rom_1 (hex, n*v repeats v):
  //   81 64 84 71 14 a1 50 3d 8a 64 35 88 72 20 3d 81 64 84 71 60 1a a1 48 64 8a 70 a4 4d 9b 59 94 84 71
  //   6c 69 81 70 64 62 23
  //   Clock
  //   Pick Addr
  //   PC+1 calculation
  //   Jump Calculation
  //   PC
  //   contents of ControlSignals (hex, n*v repeats v):
  //   23 60 23 6062 180a 402 1012 13c4 13c0 1002 1082 1102 1182 1202 1282 1302
  //   Pick ULA Input 2
  //   Immediate Sign Extension
  //   Parse Instruction
  //   Unconditional Jump Signal
  //   Pick the Detour Adrress Source
  //   Pick Register Source
  //   Pick Ula Input 1
  //   Pick Data to Write Back
  //   Control Signal Display
  //   Control Signal Parsing
endmodule
